# Fritzing sketch intval2 (saved by Fritzing 0.9.2b)
breadboards: 1

parts:
  12VDC = 2.1mm Barrel Jack with Terminal Block
  Microcontroller = Pro Trinket 5V
  S1 = H-Bridge with L298N
  Audio_Jack = Audio Jack (TRS) 3.5mm [package="PG203J [THT]"]
  Delay_Button = SWITCH-MOMENTARY-2 [package=tactile-switch-1101ne]
  Speed_Button = SWITCH-MOMENTARY-2 [package=tactile-switch-1101ne]
  Direction_Button = SWITCH-MOMENTARY-2 [package=tactile-switch-1101ne]
  LED1 = LEDs [package=led10mm]
  Microswitch = SWITCH-MOMENTARY-2 [package=tactile-switch-1101ne]
  Motor = DC Motor  # not connected

nets:
  N1: 12VDC.POS, S1.12V
  GND: 12VDC.NEG, Microcontroller.GND, S1.GND, Audio_Jack.Tip, Delay_Button.1, Speed_Button.1, Direction_Button.1, LED1.C, Microswitch.1
  N2: Microcontroller.VBAT, S1.5V
  N3: Microcontroller.D6, Direction_Button.2
  N4: Microcontroller.D5, Speed_Button.2
  N5: Microcontroller.D4, Delay_Button.2
  N6: Microcontroller.D3, Audio_Jack.Ring
  N7: Microcontroller.D9, S1.IN3
  N8: Microcontroller.D10, S1.IN4
  N9: Microcontroller.D13, LED1.A
  N10: Microcontroller.A5, Microswitch.2
  N11: S1.ENA, S1.IN1, S1.IN2, S1.M1-02, S1.M2-01, S1.M2-02, S1.ENB-5V

custom parts:
  Pro Trinket 5V: The Pro Trinket 5V is like an Arduino Pro Mini with more pins and USB included. Built with the common core Arduino chip, the ATmega328p, it has 18 GPIO, 2 extra analog inputs, 28K of flash, and 2K of RAM. It has onboard USB bootloading support with Optiboot support, so you can either program your Pro Trinket over USB or with a FTDI cable. The Pro Trinket is programmable using the Arduino IDE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
  H-Bridge with L298N: h-bridge
