# Fritzing sketch intval2_1_oshpark (saved by Fritzing 0.9.3b)
circuit board: 5.27436cm x 1.93573cm
breadboards: 1

parts:
  MOTOR = screw terminal, 2 pins
  TGR_DLY = screw terminal, 2 pins
  GND_MCR = screw terminal, 2 pins
  +5VDC- = screw terminal, 2 pins
  DIR_SPD = screw terminal, 2 pins
  intval2_1 = Arduino Nano (Rev3.0)

nets:
  N1: MOTOR.pin1, intval2_1.D10
  N2: MOTOR.pin2, intval2_1.D9
  N3: TGR_DLY.pin1, intval2_1.D4
  N4: TGR_DLY.pin2, intval2_1.D3
  N5: GND_MCR.pin1, intval2_1.A5
  N6: GND_MCR.pin2, +5VDC-.pin1, intval2_1.GND
  N7: +5VDC-.pin2, intval2_1.VIN
  N8: DIR_SPD.pin1, intval2_1.D6
  N9: DIR_SPD.pin2, intval2_1.D5

notes:
  sixteenmillimeter.com
