# Fritzing sketch intval2_oshpark (saved by Fritzing 0.9.3b)
circuit board: 3.37406cm x 1.79462cm
breadboards: 1

parts:
  intval2 = Pro Trinket 5V
  MOTOR = screw terminal, 2 pins
  TGR_DLY = screw terminal, 2 pins
  MCR_GND = screw terminal, 2 pins
  -5VDC+ = screw terminal, 2 pins
  SERVO = Dagu DGServo 9g header (male) [package=THT]
  SPD_DIR = screw terminal, 2 pins

nets:
  GND: intval2.GND, MCR_GND.pin2, -5VDC+.pin2, SERVO.gnd
  N1: intval2.VBAT, -5VDC+.pin1, SERVO.Vcc
  N2: intval2.D6, SPD_DIR.pin1
  N3: intval2.D5, SPD_DIR.pin2
  N4: intval2.D4, TGR_DLY.pin1
  N5: intval2.D3, TGR_DLY.pin2
  N6: intval2.D9, MOTOR.pin2
  N7: intval2.D10, MOTOR.pin1
  N8: intval2.D12, SERVO.pulse
  N9: intval2.A5, MCR_GND.pin1

custom parts:
  Pro Trinket 5V: The Pro Trinket 5V is like an Arduino Pro Mini with more pins and USB included. Built with the common core Arduino chip, the ATmega328p, it has 18 GPIO, 2 extra analog inputs, 28K of flash, and 2K of RAM. It has onboard USB bootloading support with Optiboot support, so you can either program your Pro Trinket over USB or with a FTDI cable. The Pro Trinket is programmable using the Arduino IDE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
