# Fritzing sketch intval2_shield (saved by Fritzing 0.9.3b)
circuit board: 8.46667cm x 5.64444cm
breadboards: 1

parts:
  Part1 = Adafruit Pro Trinket 5V 16MHz [part_number="Adafruit #2000"]
  J1 = Screw terminal - 2 pins [package=THT]
  J2 = Screw terminal - 2 pins [package=THT]
  J3 = Screw terminal - 2 pins [package=THT]
  J4 = Screw terminal - 2 pins [package=THT]
  J6 = Screw terminal - 2 pins [package=THT]
  M1 = Dagu DGServo 9g (Pan and tilt) [part_number=RS001B]

nets:
  GND: Part1.GND, J3.pin1, J4.pin1, J6.pin1, M1.gnd
  N1: Part1.VBAT, J6.pin2, M1.vcc
  N2: Part1.D6, J2.pin2
  N3: Part1.D5, J2.pin1
  N4: Part1.D4, J3.pin2
  N5: Part1.D3, J4.pin2
  N6: Part1.D9, J1.pin2
  N7: Part1.D10, J1.pin1
  N8: Part1.D12, M1.pulse

custom parts:
  Adafruit Pro Trinket 5V 16MHz: Trinket's got a big sister in town - the Pro Trinket 5V! Pro Trinket combines everything you love about Trinket with the familiarity of the common core Arduino chip, the ATmega328. It's like an Arduino Pro Mini with more pins and USB tossed in, so delicious. Trinket's a year old now, and while its been great to see tons of tiny projects, sometimes you just need more pins, more FLASH, and more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
